# Fritzing sketch sender_monitor_schema (saved by Fritzing 0.9.3b)
circuit board: 4.6cm x 3cm
breadboards: 1

parts:
  A4-5 = female pin header, 2 pins [form="♀ (female)"]
  D2-9 = female pin header, 9 pins [form="♀ (female)"]
  S1 = female pin header, 3 pins [form="♀ (female)"]
  S2 = female pin header, 3 pins [form="♀ (female)"]
  S3 = female pin header, 3 pins [form="♀ (female)"]
  S4 = female pin header, 3 pins [form="♀ (female)"]
  S5 = female pin header, 3 pins [form="♀ (female)"]
  S7 = female pin header, 3 pins [form="♀ (female)"]
  S6 = female pin header, 3 pins [form="♀ (female)"]
  RDS = female pin header, 3 pins [form="♀ (female)"]
  A0-3_D12-15 = female pin header, 9 pins [form="♀ (female)"]
  A6-7 = female pin header, 2 pins [form="♀ (female)"]
  R_R = female pin header, 3 pins [form="♀ (female)"]
  3_3v = female pin header, 4 pins [form="♀ (female)"]
  GND = female pin header, 4 pins [form="♀ (female)"]
  ULN2803a = Darlington Driver [package=dil18]

nets:
  N1: A4-5.pin1, S6.pin3
  N2: A4-5.pin2, S5.pin3
  N3: D2-9.pin1, R_R.pin2, GND.pin1, GND.pin2, GND.pin3, GND.pin4, ULN2803a.9
  N4: D2-9.pin2, ULN2803a.8
  N5: D2-9.pin3, ULN2803a.7
  N6: D2-9.pin4, ULN2803a.6
  N7: D2-9.pin5, ULN2803a.5
  N8: D2-9.pin6, ULN2803a.4
  N9: D2-9.pin7, ULN2803a.3
  N10: D2-9.pin8, ULN2803a.2
  N11: D2-9.pin9, ULN2803a.1
  N12: S1.pin1, S2.pin1, S3.pin1, S4.pin1, S5.pin1, S7.pin1, S6.pin1, RDS.pin1, A0-3_D12-15.pin1, R_R.pin1, 3_3v.pin1, 3_3v.pin2, 3_3v.pin3, 3_3v.pin4
  N13: S1.pin2, ULN2803a.11
  N14: S1.pin3, A0-3_D12-15.pin5
  N15: S2.pin2, ULN2803a.12
  N16: S2.pin3, A0-3_D12-15.pin4
  N17: S3.pin2, ULN2803a.13
  N18: S3.pin3, A0-3_D12-15.pin3
  N19: S4.pin2, ULN2803a.14
  N20: S4.pin3, A0-3_D12-15.pin2
  N21: S5.pin2, ULN2803a.15
  N22: S7.pin2, ULN2803a.17
  N23: S7.pin3, A6-7.pin2
  N24: S6.pin2, ULN2803a.16
  N25: RDS.pin2, ULN2803a.18
  N26: RDS.pin3, A0-3_D12-15.pin9
  N27: A0-3_D12-15.pin8, R_R.pin3

notes:
  RDs
  RDr
  Arduino ProMini
