# Fritzing sketch wiring schema (saved by Fritzing 0.9.3b)
circuit board: 4.66099cm x 3.03253cm
breadboards: 1

parts:
  ULN2803a = Darlington Driver [package=dil18]
  Arduino = Arduino Pro Mini (5V)
  U6 = RF-LINK_TX [package=rf-link_tx]
  Capacitive_Soil_Moisture_Sensor2 = DFRobot Capacitive Soil Moisture Sensor V1.0 [part_number=SEN0193]
  Capacitive_Soil_Moisture_Sensor3 = DFRobot Capacitive Soil Moisture Sensor V1.0 [part_number=SEN0193]
  Part1 = Arduino Nano (Rev3.0) (ICSP)
  VCC1 = Battery
  U7 = RF-LINK_RX [package=rf-link_rx]

nets:
  N1: ULN2803a.1, Arduino.D9
  N2: ULN2803a.2, Arduino.D8
  N3: ULN2803a.3, Arduino.D7
  N4: ULN2803a.4, Arduino.D6
  N5: ULN2803a.5, Arduino.D5
  N6: ULN2803a.6, Arduino.D4
  N7: ULN2803a.7, Arduino.D3
  N8: ULN2803a.8, Arduino.D2
  N9: ULN2803a.9, Arduino.GND, VCC1.-
  N10: ULN2803a.11, Capacitive_Soil_Moisture_Sensor2.GND
  N11: ULN2803a.12, Capacitive_Soil_Moisture_Sensor3.GND
  N12: ULN2803a.18, U6.GND
  VCC: Arduino.VCC, U6.+5V, Capacitive_Soil_Moisture_Sensor2.VCC, Capacitive_Soil_Moisture_Sensor3.VCC, VCC1.+
  N13: Arduino.A1, Capacitive_Soil_Moisture_Sensor3.A
  N14: Arduino.A0, Capacitive_Soil_Moisture_Sensor2.A
  N15: Arduino.D10, U6.DATA
  GND: Part1.GND, U7.GND
  N16: Part1.D11/MOSI, U7.Data
  5V: Part1.5V, U7.VCC

notes:
  RDs
  RDr
  Arduino ProMini

custom parts:
  RF-LINK_TX: Common RF transmitter of the 315.00Mhz varity
  DFRobot Capacitive Soil Moisture Sensor V1.0: DFRobot Capacitive Soil Moisture Sensor V1.0 This product measures soil moisture levels by capacitive sensing, rather than resistive sensing like other types of moisture sensor. It is made of a corrosion resistant material giving it a long service life. Insert it into soil and impress your friends with the real-time soil moisture data! The product includes an on-board voltage regulator which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
  RF-LINK_RX: RF Link receivers- WRL-8947, 8948, 8949, 8950
